// Logisim project final_circuit.circ as structural Verilog
module RAM_16x8 (
  input  Clock,
  input  [3:0] Address,
  input  Mode,
  input  CTRL,
  input  [7:0] Data_in,
  output [7:0] Data_out
);

  wire decoder_1_out0, decoder_1_out1, decoder_1_out2, decoder_1_out3, decoder_1_out4, decoder_1_out5,
       decoder_1_out6, decoder_1_out7, decoder_1_out8, decoder_1_out9, decoder_1_out10, decoder_1_out11,
       decoder_1_out12, decoder_1_out13, decoder_1_out14, decoder_1_out15;
  wire [3:0] A_M_o, A_M_o_2;
  wire [3:1] undriven;

  Byte_Reg R_0 (.Mode_RW(A_M_o[0]), .I(Data_in), .O(Data_in), .Clock(Clock), .Chip_Select(decoder_1_out0));
  Byte_Reg R_4 (.Mode_RW(A_M_o[0]), .I(Data_in), .O(Data_in), .Clock(Clock), .Chip_Select(decoder_1_out4));
  Byte_Reg R_8 (.Mode_RW(A_M_o[0]), .I(Data_in), .O(Data_in), .Clock(Clock), .Chip_Select(decoder_1_out8));
  Byte_Reg R_12 (.Mode_RW(A_M_o[0]), .I(Data_in), .O(Data_in), .Clock(Clock), .Chip_Select(decoder_1_out12));
  Byte_Reg R_1 (.Mode_RW(A_M_o[0]), .I(Data_in), .O(Data_in), .Clock(Clock), .Chip_Select(decoder_1_out1));
  Byte_Reg R_5 (.Mode_RW(A_M_o[0]), .I(Data_in), .O(Data_in), .Clock(Clock), .Chip_Select(decoder_1_out5));
  Byte_Reg R_9 (.Mode_RW(A_M_o[0]), .I(Data_in), .O(Data_in), .Clock(Clock), .Chip_Select(decoder_1_out9));
  Byte_Reg R_13 (.Mode_RW(A_M_o[0]), .I(Data_in), .O(Data_in), .Clock(Clock), .Chip_Select(decoder_1_out13));
  Byte_Reg R_2 (.Mode_RW(A_M_o[0]), .I(Data_in), .O(Data_in), .Clock(Clock), .Chip_Select(decoder_1_out2));
  Byte_Reg R_6 (.Mode_RW(A_M_o[0]), .I(Data_in), .O(Data_in), .Clock(Clock), .Chip_Select(decoder_1_out6));
  Byte_Reg R_10 (.Mode_RW(A_M_o[0]), .I(Data_in), .O(Data_in), .Clock(Clock), .Chip_Select(decoder_1_out10));
  Byte_Reg R_14 (.Mode_RW(A_M_o[0]), .I(Data_in), .O(Data_in), .Clock(Clock), .Chip_Select(decoder_1_out14));
  Byte_Reg R_3 (.Mode_RW(A_M_o[0]), .I(Data_in), .O(Data_in), .Clock(Clock), .Chip_Select(decoder_1_out3));
  Byte_Reg R_7 (.Mode_RW(A_M_o[0]), .I(Data_in), .O(Data_in), .Clock(Clock), .Chip_Select(decoder_1_out7));
  Byte_Reg R_11 (.Mode_RW(A_M_o[0]), .I(Data_in), .O(Data_in), .Clock(Clock), .Chip_Select(decoder_1_out11));
  Byte_Reg R_15 (.Mode_RW(A_M_o[0]), .I(Data_in), .O(Data_in), .Clock(Clock), .Chip_Select(decoder_1_out15));
  Decoder #(.select(4), .enable("false")) decoder_1 (
    .out0(decoder_1_out0), .out1(decoder_1_out1), .out2(decoder_1_out2), .out3(decoder_1_out3),
    .out4(decoder_1_out4), .out5(decoder_1_out5), .out6(decoder_1_out6), .out7(decoder_1_out7),
    .out8(decoder_1_out8), .out9(decoder_1_out9), .out10(decoder_1_out10), .out11(decoder_1_out11),
    .out12(decoder_1_out12), .out13(decoder_1_out13), .out14(decoder_1_out14), .out15(decoder_1_out15),
    .sel(A_M_o_2));
  Byte_Reg D (.I(Data_in), .O(Data_in), .Clock(Clock));  // open: Mode_RW, Chip_Select
  Byte_Reg A_M (.Mode_RW(CTRL), .I({Address, undriven, Mode}), .O({A_M_o_2, A_M_o}), .Clock(Clock), .Chip_Select(1'b1));

  assign Data_out = Data_in;

  // Notes on the sheet:
  //   To use less space/pieces/everything, I put Address into first 4 bits of A_M reg and Mode into the last bit
  //   However, a proper implementation of CU/sync is required
  //   Need to rewire D or D_I/O so that they do not interfere
endmodule

module Byte_Reg (
  input  [7:0] I,
  input  Clock,
  input  Mode_RW,
  input  Chip_Select,
  output [7:0] O
);

  wire and_1_out, and_2_out;
  wire [7:0] controlled_buffer_1_out, R_0_q;

  assign controlled_buffer_1_out = and_1_out ? I : 8'bz;  // Controlled_Buffer controlled_buffer_1
  and and_1 (and_1_out, Mode_RW, Chip_Select);
  and and_2 (and_2_out, Chip_Select, ~Mode_RW);  // AND_Gate
  D_Flip_Flop R_4 (.D(controlled_buffer_1_out[4]), .clk(Clock), .Q(R_0_q[4]));  // open: Qn, preset, reset
  D_Flip_Flop R_5 (.D(controlled_buffer_1_out[5]), .clk(Clock), .Q(R_0_q[5]));  // open: Qn, preset, reset
  D_Flip_Flop R_6 (.D(controlled_buffer_1_out[6]), .clk(Clock), .Q(R_0_q[6]));  // open: Qn, preset, reset
  D_Flip_Flop R_7 (.D(controlled_buffer_1_out[7]), .clk(Clock), .Q(R_0_q[7]));  // open: Qn, preset, reset
  assign O = and_2_out ? R_0_q : 8'bz;  // Controlled_Buffer controlled_buffer_2
  D_Flip_Flop R_0 (.D(controlled_buffer_1_out[0]), .clk(Clock), .Q(R_0_q[0]));  // open: Qn, preset, reset
  D_Flip_Flop R_1 (.D(controlled_buffer_1_out[1]), .clk(Clock), .Q(R_0_q[1]));  // open: Qn, preset, reset
  D_Flip_Flop R_2 (.D(controlled_buffer_1_out[2]), .clk(Clock), .Q(R_0_q[2]));  // open: Qn, preset, reset
  D_Flip_Flop R_3 (.D(controlled_buffer_1_out[3]), .clk(Clock), .Q(R_0_q[3]));  // open: Qn, preset, reset
endmodule
